// Logisim project cascadare_74163_74163.circ as structural Verilog: 1 circuit, main circuit main
module main (
  input  in_1,
  input  in_2,
  input  in_3,
  input  in_4,
  input  in_5,
  input  in_6,
  input  in_7,
  input  in_8,
  input  in_9,
  input  in_10,
  output out_11,
  output out_12,
  output out_13,
  output out_14,
  output out_15,
  output out_16,
  output out_17,
  output out_18
);

  wire clock_1_out, n74163_synch_binary_counter_1_p14;

  Clock clock_1 (.out(clock_1_out));
  // _74163__synch_binary_counter 74163_synch_binary_counter_1: pin names not known; wires that end beside it: 1'b1, 1'b1, clock_1_out, in_1, in_10, in_2, out_18, in_3, out_17, in_4, out_16, in_5, out_15, n74163_synch_binary_counter_1_p14
  // _74163__synch_binary_counter 74163_synch_binary_counter_2: pin names not known; wires that end beside it: 1'b1, n74163_synch_binary_counter_1_p14, clock_1_out, in_1, in_10, in_6, out_14, in_7, out_13, in_8, out_12, in_9, out_11

  // Other names for the same wires on the sheet: Q0 = out_18; Q1 = out_17; Q2 = out_16; Q3 = out_15; Q4 = out_14;
  //   Q5 = out_13; Q6 = out_12; Q7 = out_11
endmodule
