// Logisim project cascadare_74192_74192.circ as structural Verilog: 1 circuit, main circuit main
module main (
  input  in_1,
  input  in_2,
  input  in_3,
  input  in_4,
  input  in_5,
  input  in_6,
  input  in_7,
  input  in_8,
  input  in_9,
  input  in_10,
  input  in_11
);

  wire clock_1_out, multiplexer_1_out, multiplexer_2_out, n7447_7seg_decoder_1_p5, n7447_7seg_decoder_1_p6,
       n7447_7seg_decoder_1_p7, n7447_7seg_decoder_1_p8, n7447_7seg_decoder_1_p9, n7447_7seg_decoder_1_p10,
       n7447_7seg_decoder_1_p11, n74192_up_down_decade_counter_1_p13, n74192_up_down_decade_counter_1_p14,
       Q0, Q1, Q2, Q3, Q4, Q4_p5, Q4_p6, Q4_p7, Q4_p8, Q4_p9, Q4_p10, Q4_p11, Q5, Q6, Q7;

  Clock clock_1 (.out(clock_1_out));
  Multiplexer #(.enable("false")) multiplexer_1 (.in0(clock_1_out), .in1(1'b1), .out(multiplexer_1_out), .sel(in_10));
  Multiplexer #(.enable("false")) multiplexer_2 (.in0(1'b1), .in1(clock_1_out), .out(multiplexer_2_out), .sel(in_10));
  // _7447__7SEG_decoder 7447_7seg_decoder_1: pin names not known; wires that end beside it: Q0, Q1, Q2, Q3, n7447_7seg_decoder_1_p5, n7447_7seg_decoder_1_p6, n7447_7seg_decoder_1_p7, n7447_7seg_decoder_1_p8, n7447_7seg_decoder_1_p9, n7447_7seg_decoder_1_p10, n7447_7seg_decoder_1_p11
  // _7447__7SEG_decoder Q4: pin names not known; wires that end beside it: Q4, Q5, Q6, Q7, Q4_p5, Q4_p6, Q4_p7, Q4_p8, Q4_p9, Q4_p10, Q4_p11
  // _74192__up_down_decade_counter 74192_up_down_decade_counter_1: pin names not known; wires that end beside it: multiplexer_1_out, multiplexer_2_out, in_1, in_11, in_6, Q0, Q1, in_7, in_8, Q2, in_9, Q3, n74192_up_down_decade_counter_1_p13, n74192_up_down_decade_counter_1_p14
  _7_Segment_Display #(.active("false")) u_7_segment_display_1 (
    .g(n7447_7seg_decoder_1_p11), .f(n7447_7seg_decoder_1_p10), .a(n7447_7seg_decoder_1_p5),
    .b(n7447_7seg_decoder_1_p6), .e(n7447_7seg_decoder_1_p9), .d(n7447_7seg_decoder_1_p8),
    .c(n7447_7seg_decoder_1_p7));  // open: dp
  _7_Segment_Display #(.active("false")) u_7_segment_display_2 (
    .g(Q4_p11), .f(Q4_p10), .a(Q4_p5), .b(Q4_p6), .e(Q4_p9), .d(Q4_p8), .c(Q4_p7));  // open: dp
  // _74192__up_down_decade_counter 74192_up_down_decade_counter_2: pin names not known; wires that end beside it: n74192_up_down_decade_counter_1_p13, n74192_up_down_decade_counter_1_p14, in_1, in_11, in_11, in_2, Q4, in_3, Q5, in_4, Q6, in_5, Q7
endmodule
