// Logisim project cascadare_74193_74192.circ as structural Verilog: 1 circuit, main circuit main
module main (
  input  in_1,
  input  in_2,
  input  in_3,
  input  in_4,
  input  in_5,
  input  in_6,
  input  in_7,
  input  in_8,
  input  in_9,
  input  in_10,
  input  in_11,
  output out_12,
  output out_13,
  output out_14,
  output out_15,
  output out_16,
  output out_17,
  output out_18,
  output out_19
);

  wire clock_1_out, multiplexer_1_out, multiplexer_2_out, n74193_up_down_binary_counter_1_p13,
       n74193_up_down_binary_counter_1_p14;

  Clock clock_1 (.out(clock_1_out));
  Multiplexer #(.enable("false")) multiplexer_1 (.in0(clock_1_out), .in1(1'b1), .out(multiplexer_1_out), .sel(in_10));
  Multiplexer #(.enable("false")) multiplexer_2 (.in0(1'b1), .in1(clock_1_out), .out(multiplexer_2_out), .sel(in_10));
  // _74193__up_down_binary_counter 74193_up_down_binary_counter_1: pin names not known; wires that end beside it: multiplexer_1_out, multiplexer_2_out, in_1, in_11, in_6, out_19, in_7, out_18, in_8, out_17, in_9, out_16, n74193_up_down_binary_counter_1_p13, n74193_up_down_binary_counter_1_p14
  // _74192__up_down_decade_counter 74192_up_down_decade_counter_1: pin names not known; wires that end beside it: n74193_up_down_binary_counter_1_p13, n74193_up_down_binary_counter_1_p14, in_1, in_11, out_15, in_2, in_3, out_14, in_4, out_13, in_5, out_12

  // Other names for the same wires on the sheet: Q0 = out_19; Q1 = out_18; Q2 = out_17; Q3 = out_16; Q4 = out_15;
  //   Q5 = out_14; Q6 = out_13; Q7 = out_12
endmodule
